// Logisim project BorzaSebastianLogisim.circ as structural Verilog: 1 circuit, main circuit main
module main (
  input  A,
  input  B,
  input  C,
  input  D
);

  wire A_prime_BC_prime_2_out, A_prime_BC_prime_out, A_prime_BD_prime_out, A_prime_CD_out, B_out,
       B_prime_C_out, B_prime_D_prime_2_out, B_prime_D_prime_out, BC_prime_D_out, BD_out, BL_out, BR_out,
       C_prime_D_prime_out, CD_prime_out, M_out, not_1_out, not_2_out, not_3_out, not_4_out, T_out, TL_out,
       TR_out;

  not not_1 (not_1_out, A);
  not not_2 (not_2_out, B);
  not not_3 (not_3_out, C);
  not not_4 (not_4_out, D);
  and BD (BD_out, B, D);
  and B_prime_D_prime (B_prime_D_prime_out, not_2_out, not_4_out);
  and A_prime_CD (A_prime_CD_out, not_1_out, C, D, D);
  and A_prime_BC_prime (A_prime_BC_prime_out, not_1_out, not_3_out, B);
  and A_prime_BD_prime (A_prime_BD_prime_out, not_1_out, B, not_4_out);
  and C_prime_D_prime (C_prime_D_prime_out, not_3_out, not_4_out);
  and B_prime_D_prime_2 (B_prime_D_prime_2_out, not_4_out, not_2_out);
  and BC_prime_D (BC_prime_D_out, B, not_3_out, D);
  and B_prime_C (B_prime_C_out, not_2_out, C);
  and CD_prime (CD_prime_out, C, not_4_out);
  and A_prime_BC_prime_2 (A_prime_BC_prime_2_out, not_3_out, not_1_out, B);
  or T (T_out, BD_out, A, C, B_prime_D_prime_out);
  or TR (TR_out, A, not_2_out, C_prime_D_prime_out, A_prime_CD_out);
  or M (M_out, A, B_prime_C_out, CD_prime_out, A_prime_BC_prime_2_out);
  or TL (TL_out, A, A_prime_BD_prime_out, C_prime_D_prime_out, A_prime_BC_prime_out);
  or BL (BL_out, CD_prime_out, B_prime_D_prime_2_out);
  or u_B (B_out, A, B_prime_C_out, B_prime_D_prime_2_out, BC_prime_D_out, CD_prime_out);
  or BR (BR_out, A, B, not_3_out, D);
  _7_Segment_Display u_7_segment_display_1 (
    .g(M_out), .f(TL_out), .a(T_out), .b(TR_out), .e(BL_out), .d(B_out), .c(BR_out));  // open: dp
endmodule
